// Logisim project pipeline_processor phase2 (final edit).circ as structural Verilog: 18 circuits, main circuit Register File
module Register_File (
  input  [2:0] Write_Register,
  input  [2:0] Read_Register_1,
  input  [2:0] Read_Register_2,
  input  [15:0] Write_Data,
  input  Register_Write,
  output [15:0] Read_Data_1,
  output [15:0] Read_Data_2,
  output [15:0] R1,
  output [15:0] R2,
  output [15:0] R3,
  output [15:0] R4,
  output [15:0] R5,
  output [15:0] R6,
  output [15:0] R7
);

  wire and_1_out, and_2_out, and_3_out, and_4_out, and_5_out, and_6_out, and_7_out, Clock_out,
       decoder_1_out1, decoder_1_out2, decoder_1_out3, decoder_1_out4, decoder_1_out5, decoder_1_out6,
       decoder_1_out7, undriven;

  Decoder #(.select(3), .enable("false")) decoder_1 (
    .out1(decoder_1_out1), .out2(decoder_1_out2), .out3(decoder_1_out3), .out4(decoder_1_out4),
    .out5(decoder_1_out5), .out6(decoder_1_out6), .out7(decoder_1_out7), .sel(Write_Register));  // open: out0
  and and_1 (and_1_out, decoder_1_out1, Register_Write);
  and and_2 (and_2_out, decoder_1_out2, Register_Write);
  and and_3 (and_3_out, decoder_1_out3, Register_Write);
  and and_4 (and_4_out, decoder_1_out4, Register_Write);
  and and_5 (and_5_out, decoder_1_out5, Register_Write);
  and and_6 (and_6_out, decoder_1_out6, Register_Write);
  and and_7 (and_7_out, decoder_1_out7, Register_Write);
  Register #(.width(16), .trigger("falling")) register_1 (
    .D(Write_Data), .en(and_1_out), .Q(R1), .clk(Clock_out));  // open: clr
  Register #(.width(16), .trigger("falling")) register_2 (
    .D(Write_Data), .en(and_2_out), .Q(R2), .clk(Clock_out), .clr(undriven));
  Register #(.width(16), .trigger("falling")) register_3 (
    .D(Write_Data), .en(and_3_out), .Q(R3), .clk(Clock_out));  // open: clr
  Register #(.width(16), .trigger("falling")) register_4 (
    .D(Write_Data), .en(and_4_out), .Q(R4), .clk(Clock_out));  // open: clr
  Register #(.width(16), .trigger("falling")) register_5 (
    .D(Write_Data), .en(and_5_out), .Q(R5), .clk(Clock_out));  // open: clr
  Register #(.width(16), .trigger("falling")) register_6 (
    .D(Write_Data), .en(and_6_out), .Q(R6), .clk(Clock_out));  // open: clr
  Register #(.width(16), .trigger("falling")) register_7 (
    .D(Write_Data), .en(and_7_out), .Q(R7), .clk(Clock_out));  // open: clr
  Clock Clock (.out(Clock_out));
  Multiplexer #(.select(3), .width(16)) multiplexer_1 (
    .in0({16{1'b0}}), .in1(R1), .in2(R2), .in3(R3), .in4(R4), .in5(R5), .in6(R6), .in7(R7),
    .out(Read_Data_1), .sel(Read_Register_1));  // open: en
  Multiplexer #(.select(3), .width(16), .enable("false")) multiplexer_2 (
    .in0({16{1'b0}}), .in1(R1), .in2(R2), .in3(R3), .in4(R4), .in5(R5), .in6(R6), .in7(R7),
    .out(Read_Data_2), .sel(Read_Register_2));
endmodule

module ALU (
  input  [15:0] A,
  input  [15:0] B,
  input  [3:0] func,
  output zeroFlag,
  output [15:0] R
);

  wire comparator_1_lt, comparator_2_lt, comparator_3_eq, comparator_4_eq, comparator_5_eq, comparator_5_gt,
       not_1_out, or_2_out;
  wire [15:0] adder_1_out, and_1_out, bit_extender_1_out, bit_extender_2_out, bit_extender_3_out,
       bit_extender_4_out, bit_extender_5_out, nor_1_out, or_1_out, shifter_1_out, shifter_2_out,
       shifter_3_out, shifter_4_out, subtractor_1_out, xor_1_out;

  assign and_1_out = A & B;  // AND_Gate and_1, 16 bits wide
  assign or_1_out = A | B;  // OR_Gate or_1, 16 bits wide
  assign xor_1_out = A ^ B;  // XOR_Gate xor_1, 16 bits wide
  assign nor_1_out = ~(A | B);  // NOR_Gate nor_1, 16 bits wide
  Adder #(.width(16)) adder_1 (.a(A), .b(B), .out(adder_1_out));  // open: cin, cout
  Subtractor #(.width(16)) subtractor_1 (.a(A), .b(B), .out(subtractor_1_out));  // open: bin, bout
  Comparator #(.width(16)) comparator_1 (.a(A), .b(B), .lt(comparator_1_lt));  // open: gt, eq
  Comparator #(.width(16), .mode("unsigned")) comparator_2 (.a(A), .b(B), .lt(comparator_2_lt));  // open: gt, eq
  Comparator #(.width(16)) comparator_3 (.a(A), .b(B), .eq(comparator_3_eq));  // open: gt, lt
  Comparator #(.width(16)) comparator_4 (.a(A), .b(B), .eq(comparator_4_eq));  // open: gt, lt
  Comparator #(.width(16)) comparator_5 (.a(A), .b(B), .gt(comparator_5_gt), .eq(comparator_5_eq));  // open: lt
  not not_1 (not_1_out, comparator_4_eq);
  or or_2 (or_2_out, comparator_5_gt, comparator_5_eq);
  Shifter #(.width(16)) shifter_1 (.in(A), .\dist (B[3:0]), .out(shifter_1_out));
  Shifter #(.width(16), .shift("lr")) shifter_2 (.in(A), .\dist (B[3:0]), .out(shifter_2_out));
  Shifter #(.width(16), .shift("ar")) shifter_3 (.in(A), .\dist (B[3:0]), .out(shifter_3_out));
  Shifter #(.width(16), .shift("rr")) shifter_4 (.in(A), .\dist (B[3:0]), .out(shifter_4_out));
  assign bit_extender_1_out = {{15{1'b0}}, comparator_1_lt};  // Bit_Extender bit_extender_1
  assign bit_extender_2_out = {{15{1'b0}}, comparator_2_lt};  // Bit_Extender bit_extender_2
  assign bit_extender_3_out = {{15{1'b0}}, comparator_3_eq};  // Bit_Extender bit_extender_3
  assign bit_extender_4_out = {{15{1'b0}}, not_1_out};  // Bit_Extender bit_extender_4
  assign bit_extender_5_out = {{15{1'b0}}, or_2_out};  // Bit_Extender bit_extender_5
  nor nor_2 (zeroFlag, subtractor_1_out[0], subtractor_1_out[1], subtractor_1_out[2], subtractor_1_out[3], subtractor_1_out[4], subtractor_1_out[5], subtractor_1_out[6], subtractor_1_out[7], subtractor_1_out[8], subtractor_1_out[9], subtractor_1_out[10], subtractor_1_out[11], subtractor_1_out[12], subtractor_1_out[13], subtractor_1_out[14], subtractor_1_out[15]);
  Multiplexer #(.select(4), .width(16), .enable("false")) multiplexer_1 (
    .in0(and_1_out), .in1(or_1_out), .in2(xor_1_out), .in3(nor_1_out), .in4(adder_1_out),
    .in5(subtractor_1_out), .in6(bit_extender_1_out), .in7(bit_extender_2_out), .in8(shifter_1_out),
    .in9(shifter_2_out), .in10(shifter_3_out), .in11(shifter_4_out), .in12(bit_extender_3_out),
    .in13(bit_extender_4_out), .in14(bit_extender_1_out), .in15(bit_extender_5_out), .out(R), .sel(func));

  // Notes on the sheet:
  //   SLT/BLT
  //   SLTU
  //   branch ==
  //   branch !=
  //   BGE
endmodule

module ALUCtrl (
  input  OP4,
  input  OP3,
  input  OP2,
  input  OP1,
  input  OP0,
  input  F1,
  input  F0,
  output ALU3,
  output ALU2,
  output ALU1,
  output ALU0
);

  wire and_1_out, and_2_out, and_3_out, and_4_out, and_5_out, and_6_out, and_7_out, and_8_out, and_9_out,
       and_10_out, and_11_out, and_12_out, and_13_out, not_1_out, not_2_out, not_3_out, not_4_out, not_5_out,
       not_6_out, not_7_out, not_8_out, not_9_out, not_10_out, not_11_out, not_12_out, not_13_out,
       not_14_out, not_15_out;

  not not_1 (not_1_out, OP2);
  not not_2 (not_2_out, OP3);
  not not_3 (not_3_out, OP2);
  not not_4 (not_4_out, OP3);
  not not_5 (not_5_out, OP3);
  not not_6 (not_6_out, OP2);
  not not_7 (not_7_out, OP3);
  not not_8 (not_8_out, OP0);
  not not_9 (not_9_out, OP2);
  not not_10 (not_10_out, OP4);
  not not_11 (not_11_out, OP3);
  not not_12 (not_12_out, OP2);
  not not_13 (not_13_out, OP3);
  not not_14 (not_14_out, OP1);
  not not_15 (not_15_out, OP2);
  and and_1 (and_1_out, OP3, not_1_out);
  and and_2 (and_2_out, OP3, OP1);
  and and_3 (and_3_out, not_2_out, not_3_out, OP0);
  and and_4 (and_4_out, not_4_out, OP1, OP0);
  and and_5 (and_5_out, OP3, OP2);
  and and_6 (and_6_out, not_5_out, not_6_out, F1);
  and and_7 (and_7_out, not_7_out, OP1, not_8_out);
  and and_8 (and_8_out, not_9_out, OP1);
  and and_9 (and_9_out, not_10_out, not_11_out, not_12_out, F0);
  and and_10 (and_10_out, not_13_out, OP2, not_14_out, OP0);
  and and_11 (and_11_out, OP3, not_15_out, OP0);
  and and_12 (and_12_out, OP3, OP1, OP0);
  and and_13 (and_13_out, OP4, OP0);
  or or_1 (ALU3, and_1_out, and_2_out, OP4);
  or or_2 (ALU2, and_3_out, and_4_out, and_5_out, OP4);
  or or_3 (ALU1, and_6_out, and_7_out, and_8_out, OP4);
  or or_4 (ALU0, and_9_out, and_10_out, and_11_out, and_12_out, and_13_out);
endmodule

module ControlUnit (
  input  OP5,
  input  OP4,
  input  OP3,
  input  OP2,
  input  OP1,
  output RegDst1,
  output RegDst0,
  output RegWr,
  output AluSrc,
  output MemRd,
  output MemWr,
  output memToReg1,
  output memToReg0,
  output BSelector2,
  output BSelector1,
  output BSelector0
);

  wire and_2_out, and_3_out, and_4_out, and_5_out, and_6_out, and_7_out, and_8_out, and_9_out, and_10_out,
       and_11_out, and_14_out, and_15_out, and_16_out, and_17_out, and_18_out, and_19_out, and_20_out,
       and_21_out, and_22_out, not_1_out, not_2_out, not_3_out, not_4_out, not_5_out, not_6_out, not_7_out,
       not_8_out, not_9_out, not_10_out, not_11_out, not_12_out, not_13_out, not_14_out, not_15_out,
       not_16_out, not_17_out, not_18_out, not_19_out, not_20_out, not_21_out, not_22_out, not_23_out,
       not_24_out, not_25_out, not_26_out, not_27_out, not_28_out, not_29_out, not_30_out, not_31_out,
       not_32_out, not_33_out, not_34_out;

  not not_1 (not_1_out, OP4);
  not not_2 (not_2_out, OP3);
  not not_3 (not_3_out, OP5);
  not not_4 (not_4_out, OP4);
  not not_5 (not_5_out, OP2);
  not not_6 (not_6_out, OP5);
  not not_7 (not_7_out, OP2);
  not not_8 (not_8_out, OP1);
  not not_9 (not_9_out, OP5);
  not not_10 (not_10_out, OP4);
  not not_11 (not_11_out, OP5);
  not not_12 (not_12_out, OP3);
  not not_13 (not_13_out, OP4);
  not not_14 (not_14_out, OP3);
  not not_15 (not_15_out, OP1);
  not not_16 (not_16_out, OP4);
  not not_17 (not_17_out, OP3);
  not not_18 (not_18_out, OP2);
  not not_19 (not_19_out, OP5);
  not not_20 (not_20_out, OP2);
  not not_21 (not_21_out, OP1);
  not not_22 (not_22_out, OP5);
  not not_23 (not_23_out, OP2);
  not not_24 (not_24_out, OP2);
  not not_25 (not_25_out, OP4);
  not not_26 (not_26_out, OP5);
  not not_27 (not_27_out, OP4);
  not not_28 (not_28_out, OP5);
  not not_29 (not_29_out, OP2);
  not not_30 (not_30_out, OP4);
  not not_31 (not_31_out, OP3);
  not not_32 (not_32_out, OP4);
  not not_33 (not_33_out, OP1);
  not not_34 (not_34_out, OP5);
  not not_35 (BSelector0, OP1);
  and and_1 (RegDst0, not_1_out, not_2_out);
  and and_2 (and_2_out, not_3_out, not_4_out, not_5_out);
  and and_3 (and_3_out, not_6_out, not_7_out, not_8_out);
  and and_4 (and_4_out, not_9_out, not_10_out, OP3);
  and and_5 (and_5_out, not_11_out, OP4, not_12_out);
  and and_6 (and_6_out, OP5, not_13_out, not_14_out, OP2, not_15_out);
  and and_7 (and_7_out, OP5, OP4, OP3, OP2, OP1);
  and and_8 (and_8_out, not_16_out, OP3);
  and and_9 (and_9_out, OP4, not_17_out);
  and and_10 (and_10_out, OP4, not_18_out);
  and and_11 (and_11_out, OP5, OP2);
  and and_12 (MemRd, not_19_out, OP4, OP3, not_20_out, not_21_out);
  and and_13 (MemWr, not_22_out, OP4, OP3, not_23_out, OP1);
  and and_14 (and_14_out, OP4, OP3, not_24_out);
  and and_15 (and_15_out, OP5, not_25_out);
  and and_16 (and_16_out, not_26_out, not_27_out);
  and and_17 (and_17_out, not_28_out, not_29_out);
  and and_18 (and_18_out, not_30_out, OP2);
  and and_19 (and_19_out, OP4, not_31_out);
  and and_20 (and_20_out, OP5, OP3);
  and and_21 (and_21_out, not_32_out, not_33_out);
  and and_22 (and_22_out, not_34_out, OP1);
  or or_1 (RegWr, and_2_out, and_3_out, and_4_out, and_5_out, and_6_out, and_7_out);
  or or_2 (AluSrc, and_8_out, and_9_out, and_10_out, and_11_out);
  or or_3 (memToReg0, and_14_out, and_15_out);
  or or_4 (BSelector2, and_16_out, and_17_out, and_18_out, and_19_out, and_20_out);
  or or_5 (BSelector1, and_21_out, and_22_out);

  assign memToReg1 = OP5;
  assign RegDst1 = OP5;
endmodule

module signals (
  input  op4,
  input  op3,
  input  op2,
  input  op1,
  input  op0,
  input  fun1,
  input  fun0,
  output J,
  output JAL,
  output JR,
  output LUI
);

  wire not_1_out, not_2_out, not_3_out, not_4_out, not_5_out, not_6_out, not_7_out, not_8_out, not_9_out,
       not_10_out;

  not not_1 (not_1_out, op0);
  and and_1 (JAL, op4, op3, op2, op1, op0);
  not not_2 (not_2_out, op4);
  not not_3 (not_3_out, op3);
  not not_4 (not_4_out, op2);
  not not_5 (not_5_out, op0);
  not not_6 (not_6_out, fun1);
  not not_7 (not_7_out, fun0);
  not not_8 (not_8_out, op3);
  not not_9 (not_9_out, op2);
  not not_10 (not_10_out, op0);
  and and_2 (J, op4, op3, op2, op1, not_1_out);
  and and_3 (JR, not_2_out, not_3_out, not_4_out, op1, not_5_out, not_6_out, not_7_out);
  and and_4 (LUI, op4, not_8_out, not_9_out, op1, not_10_out);
endmodule

// PC
module PC_Counter (
  input  [15:0] busA__load_store,
  input  [4:0] Imm,
  input  clk,
  input  [10:0] jump_0_10,
  input  [15:0] PC_ID,
  input  branch_or_pc_1,
  input  [4:0] OPcode,
  input  disable_PC,
  input  [1:0] fun,
  output [15:0] PC_plus_1,
  output [15:0] PC_value,
  output flush
);

  wire and_1_out, and_2_out, not_1_out, not_2_out, or_2_out, signals_1_j, signals_1_jal;
  wire [1:0] Jsignals;
  wire [15:0] adder_1_out, adder_2_out, bit_extender_1_out, bit_extender_2_out, multiplexer_1_out,
       multiplexer_2_out;

  assign bit_extender_1_out = {{11{Imm[4]}}, Imm};  // Bit_Extender bit_extender_1
  Adder #(.width(16)) adder_1 (.a(bit_extender_1_out), .b(PC_ID), .out(adder_1_out));  // open: cin, cout
  Multiplexer #(.width(16), .enable("false")) multiplexer_1 (
    .in0(PC_plus_1), .in1(adder_1_out), .out(multiplexer_1_out), .sel(branch_or_pc_1));
  assign bit_extender_2_out = {{5{jump_0_10[10]}}, jump_0_10};  // Bit_Extender bit_extender_2
  signals signals_1 (
    .op4(OPcode[4]), .op3(OPcode[3]), .op2(OPcode[2]), .op1(OPcode[1]), .op0(OPcode[0]), .fun1(fun[0]),
    .fun0(fun[1]), .J(signals_1_j), .JAL(signals_1_jal), .JR(Jsignals[0]));  // open: LUI
  Adder #(.width(16)) adder_2 (.a(bit_extender_2_out), .b(PC_ID), .out(adder_2_out));  // open: cin, cout
  or or_1 (Jsignals[1], signals_1_j, signals_1_jal);
  Multiplexer #(.select(2), .width(16)) multiplexer_2 (
    .in0(multiplexer_1_out), .in1(busA__load_store), .in2(adder_2_out), .out(multiplexer_2_out),
    .sel(Jsignals), .en(not_1_out));  // open: in3
  Register #(.width(16)) register_1 (.D(multiplexer_2_out), .Q(PC_value), .clk(clk));  // open: en, clr
  not not_1 (not_1_out, disable_PC);
  Adder #(.width(16)) adder_3 (.a(16'h1), .b(PC_value), .out(PC_plus_1));  // open: cin, cout
  not not_2 (not_2_out, branch_or_pc_1);
  or or_2 (or_2_out, Jsignals[0], Jsignals[1]);
  and and_1 (and_1_out, branch_or_pc_1, not_1_out);
  and and_2 (and_2_out, or_2_out, not_2_out);
  or or_3 (flush, and_2_out, and_1_out);

  // Other names for the same wires on the sheet: branch = branch_or_pc_1

  // Notes on the sheet:
  //   branch , next pc
  //   JR
  //   JAL J
endmodule

module LUI (
  input  [15:0] jump_0_10,
  output [15:0] out_2
);

  // Probe on out_2
  Shifter #(.width(16)) shifter_1 (.in(jump_0_10), .\dist (4'b0101), .out(out_2));
endmodule

// extend
module extend_signal (
  input  OP4,
  input  OP3,
  input  OP2,
  input  OP1,
  input  OP0,
  output Extsignal
);

  wire and_1_out, and_2_out, not_1_out, not_2_out, not_3_out, not_4_out, not_5_out, not_6_out;

  not not_1 (not_1_out, OP4);
  not not_2 (not_2_out, OP3);
  not not_3 (not_3_out, OP1);
  not not_4 (not_4_out, OP4);
  not not_5 (not_5_out, OP3);
  not not_6 (not_6_out, OP0);
  and and_1 (and_1_out, not_1_out, not_2_out, OP2, not_3_out);
  and and_2 (and_2_out, not_4_out, not_5_out, OP2, not_6_out);
  or or_1 (Extsignal, and_1_out, and_2_out);
endmodule

module IF_ID_Reg (
  input  [15:0] instruction,
  input  [15:0] PC,
  input  IF_Flash,
  input  clock,
  input  IF_ID_RegEnable,
  output [15:0] instruction_2,
  output [15:0] PC1
);

  wire not_1_out;
  wire [15:0] multiplexer_1_out, multiplexer_2_out;

  Multiplexer #(.width(16)) multiplexer_1 (
    .in0(instruction), .in1({16{1'b0}}), .out(multiplexer_1_out), .sel(IF_Flash), .en(not_1_out));
  Multiplexer #(.width(16)) multiplexer_2 (
    .in0(PC), .in1({16{1'b0}}), .out(multiplexer_2_out), .sel(IF_Flash), .en(not_1_out));
  not not_1 (not_1_out, IF_ID_RegEnable);
  Register #(.width(16)) register_1 (.D(multiplexer_1_out), .Q(instruction_2), .clk(clock));  // open: en, clr
  Register #(.width(16)) register_2 (.D(multiplexer_2_out), .Q(PC1), .clk(clock));  // open: en, clr
endmodule

module ID_EX_Reg (
  input  [15:0] PC1,
  input  [15:0] LUI,
  input  [1:0] RegDst,
  input  ALUSrc,
  input  [15:0] BUSA,
  input  RegWr,
  input  [15:0] BUSB,
  input  MemRd,
  input  MemWr,
  input  [2:0] Rd1,
  input  [1:0] MemtoReg,
  input  [15:0] Imm,
  input  [3:0] Alu_op,
  input  [2:0] Rs,
  input  [2:0] Rt,
  input  in_16,
  output [15:0] PC2,
  output [15:0] LUI_2,
  output [1:0] RegDst_2,
  output [15:0] BUSA_2,
  output ALUSrc_2,
  output RegWr_2,
  output [15:0] BUSB_2,
  output MemRd_2,
  output MemWr_2,
  output [2:0] Rd1_2,
  output [1:0] MemtoReg_2,
  output [15:0] Imm_2,
  output [3:0] Alu_op_2,
  output [2:0] Rs_2,
  output [2:0] Rt_2
);

  Register #(.width(16)) register_1 (.D(PC1), .en(1'b1), .Q(PC2), .clk(in_16));  // open: clr
  Register #(.width(16)) register_2 (.D(LUI), .en(1'b1), .Q(LUI_2), .clk(in_16));  // open: clr
  Register #(.width(16)) register_3 (.D(BUSA), .en(1'b1), .Q(BUSA_2), .clk(in_16));  // open: clr
  Register #(.width(16)) register_4 (.D(BUSB), .en(1'b1), .Q(BUSB_2), .clk(in_16));  // open: clr
  Register #(.width(3)) register_5 (.D(Rd1), .en(1'b1), .Q(Rd1_2), .clk(in_16));  // open: clr
  Register #(.width(16)) register_6 (.D(Imm), .en(1'b1), .Q(Imm_2), .clk(in_16));  // open: clr
  Register #(.width(3)) register_7 (.D(Rs), .en(1'b1), .Q(Rs_2), .clk(in_16));  // open: clr
  Register #(.width(3)) register_8 (.D(Rt), .en(1'b1), .Q(Rt_2), .clk(in_16));  // open: clr
  Register #(.width(2)) register_9 (.D(RegDst), .en(1'b1), .Q(RegDst_2), .clk(in_16));  // open: clr
  Register #(.width(1)) register_10 (.D(ALUSrc), .en(1'b1), .Q(ALUSrc_2), .clk(in_16));  // open: clr
  Register #(.width(1)) register_11 (.D(RegWr), .en(1'b1), .Q(RegWr_2), .clk(in_16));  // open: clr
  Register #(.width(1)) register_12 (.D(MemRd), .en(1'b1), .Q(MemRd_2), .clk(in_16));  // open: clr
  Register #(.width(1)) register_13 (.D(MemWr), .en(1'b1), .Q(MemWr_2), .clk(in_16));  // open: clr
  Register #(.width(2)) register_14 (.D(MemtoReg), .en(1'b1), .Q(MemtoReg_2), .clk(in_16));  // open: clr
  Register #(.width(4)) register_15 (.D(Alu_op), .en(1'b1), .Q(Alu_op_2), .clk(in_16));  // open: clr
endmodule

module EX_DM_Reg (
  input  clk,
  input  [15:0] ALU_Result,
  input  [1:0] RegDst,
  input  [2:0] Rd2,
  input  RegWr,
  input  [15:0] Bus_B,
  input  MemRd,
  input  [15:0] PC3,
  input  MemWr,
  input  [15:0] LUI,
  input  [1:0] MemtoReg,
  input  [15:0] Data_Load_2,
  output [15:0] ALU_Result_2,
  output [1:0] RegDst_2,
  output [2:0] Rd2_2,
  output RegWr_2,
  output [15:0] Bus_B_2,
  output MemRd_2,
  output [15:0] PC4,
  output MemWr_2,
  output [15:0] LUI_2,
  output [1:0] MemtoReg_2,
  output [15:0] Data_Load_3
);

  Register #(.width(16)) register_1 (.D(ALU_Result), .en(1'b1), .Q(ALU_Result_2), .clk(clk));  // open: clr
  Register #(.width(3)) register_2 (.D(Rd2), .en(1'b1), .Q(Rd2_2), .clk(clk));  // open: clr
  Register #(.width(16)) register_3 (.D(Bus_B), .en(1'b1), .Q(Bus_B_2), .clk(clk));  // open: clr
  Register #(.width(16)) register_4 (.D(PC3), .en(1'b1), .Q(PC4), .clk(clk));  // open: clr
  Register #(.width(16)) register_5 (.D(LUI), .en(1'b1), .Q(LUI_2), .clk(clk));  // open: clr
  Register #(.width(16)) register_6 (.D(Data_Load_2), .en(1'b1), .Q(Data_Load_3), .clk(clk));  // open: clr
  Register #(.width(2)) register_7 (.D(RegDst), .en(1'b1), .Q(RegDst_2), .clk(clk));  // open: clr
  Register #(.width(1)) register_8 (.D(RegWr), .en(1'b1), .Q(RegWr_2), .clk(clk));  // open: clr
  Register #(.width(1)) register_9 (.D(MemRd), .en(1'b1), .Q(MemRd_2), .clk(clk));  // open: clr
  Register #(.width(1)) register_10 (.D(MemWr), .en(1'b1), .Q(MemWr_2), .clk(clk));  // open: clr
  Register #(.width(2)) register_11 (.D(MemtoReg), .en(1'b1), .Q(MemtoReg_2), .clk(clk));  // open: clr
endmodule

module DM_WB_Reg (
  input  clk,
  input  [15:0] DataW,
  input  [2:0] Rd3,
  input  RegWr,
  output [15:0] DataW_2,
  output [2:0] Rd3_2,
  output RegWr_2
);

  Register #(.width(16)) register_1 (.D(DataW), .en(1'b1), .Q(DataW_2), .clk(clk));  // open: clr
  Register #(.width(3)) register_2 (.D(Rd3), .en(1'b1), .Q(Rd3_2), .clk(clk));  // open: clr
  Register #(.width(1)) register_3 (.D(RegWr), .en(1'b1), .Q(RegWr_2), .clk(clk));  // open: clr
endmodule

module branch_unit (
  input  [15:0] BusA,
  input  [2:0] branchSelector,
  input  [15:0] BusB,
  output Branch_enable
);

  wire comparator_1_eq, comparator_1_gt, comparator_1_lt, not_1_out, or_1_out;

  Comparator #(.width(16)) comparator_1 (
    .a(BusA), .b(BusB), .gt(comparator_1_gt), .eq(comparator_1_eq), .lt(comparator_1_lt));
  or or_1 (or_1_out, comparator_1_gt, comparator_1_eq);
  not not_1 (not_1_out, comparator_1_eq);
  Multiplexer #(.select(3), .enable("false")) multiplexer_1 (
    .in0(or_1_out), .in1(comparator_1_eq), .in2(not_1_out), .in3(comparator_1_lt), .in4(1'b0), .in5(1'b0),
    .in6(1'b0), .in7(1'b0), .out(Branch_enable), .sel(branchSelector));

  // Notes on the sheet:
  //   BGE
  //   BEQ
  //   BNE
  //   BLT
endmodule

module Forward_Unit (
  input  [2:0] ID_EX_RS2,
  input  [2:0] EXE_MEM_RD3,
  input  EX_MEM_REG_WR,
  input  [2:0] ID_EX_RT2,
  input  [2:0] WB_RD4,
  input  MEM_WB_REG_WR,
  output [1:0] FORWARDA,
  output [1:0] out_8
);

  wire and_1_out, and_2_out, and_5_out, and_6_out, comparator_1_eq, comparator_2_eq, comparator_3_eq,
       comparator_4_eq, comparator_5_eq, comparator_6_eq, not_1_out, not_2_out;

  Comparator #(.width(3), .mode("unsigned")) comparator_1 (
    .a(EXE_MEM_RD3), .b(3'b000), .eq(comparator_1_eq));  // open: gt, lt
  not not_1 (not_1_out, comparator_1_eq);
  Comparator #(.width(3), .mode("unsigned")) comparator_2 (
    .a(WB_RD4), .b(3'b000), .eq(comparator_2_eq));  // open: gt, lt
  Comparator #(.width(3)) comparator_3 (.a(ID_EX_RS2), .b(EXE_MEM_RD3), .eq(comparator_3_eq));  // open: gt, lt
  and and_1 (and_1_out, not_1_out, EX_MEM_REG_WR);
  Comparator #(.width(3)) comparator_4 (.a(EXE_MEM_RD3), .b(ID_EX_RT2), .eq(comparator_4_eq));  // open: gt, lt
  Comparator #(.width(3)) comparator_5 (.a(ID_EX_RS2), .b(WB_RD4), .eq(comparator_5_eq));  // open: gt, lt
  not not_2 (not_2_out, comparator_2_eq);
  and and_2 (and_2_out, not_2_out, MEM_WB_REG_WR);
  Comparator #(.width(3)) comparator_6 (.a(WB_RD4), .b(ID_EX_RT2), .eq(comparator_6_eq));  // open: gt, lt
  and and_3 (FORWARDA[0], comparator_3_eq, and_1_out);
  and and_4 (out_8[0], and_1_out, comparator_4_eq);
  and and_5 (and_5_out, comparator_5_eq, and_2_out);
  and and_6 (and_6_out, and_2_out, comparator_6_eq);
  and and_7 (FORWARDA[1], and_5_out, ~FORWARDA[0]);  // AND_Gate
  and and_8 (out_8[1], and_6_out, ~out_8[0]);  // AND_Gate

  // Other names for the same wires on the sheet: FORWARDA_01 = FORWARDA[0]; FORWARDB_01 = out_8[0];
  //   RS[2:0] = ID_EX_RS2; RT[2:0] = ID_EX_RT2

  // Notes on the sheet:
  //   FORWARDB=10
endmodule

module stall (
  input  [2:0] Rs,
  input  [4:0] OPcode,
  input  [2:0] RD2,
  input  [2:0] Rt,
  input  IF_ID_ALUSrc,
  output IF_ID_RegEnable,
  output Disable_PC,
  output zero_signals
);

  wire and_1_out, and_2_out, comparator_1_eq, comparator_2_eq, comparator_3_eq, comparator_4_eq,
       decoder_1_out14, decoder_1_out15, decoder_1_out16, decoder_1_out17, not_1_out, stall;

  Comparator #(.width(3), .mode("unsigned")) comparator_1 (.a(RD2), .b(3'b000), .eq(comparator_1_eq));  // open: gt, lt
  Comparator #(.width(3)) comparator_2 (.a(Rs), .b(RD2), .eq(comparator_2_eq));  // open: gt, lt
  not not_1 (not_1_out, comparator_1_eq);
  Comparator #(.width(3)) comparator_3 (.a(RD2), .b(Rt), .eq(comparator_3_eq));  // open: gt, lt
  Comparator #(.width(1)) comparator_4 (.a(IF_ID_ALUSrc), .b(1'b0), .eq(comparator_4_eq));  // open: gt, lt
  and and_1 (and_1_out, comparator_2_eq, stall, not_1_out);
  and and_2 (and_2_out, stall, not_1_out, comparator_3_eq, comparator_4_eq);
  or or_1 (Disable_PC, and_1_out, and_2_out);
  Decoder #(.select(5)) decoder_1 (
    .out14(decoder_1_out14), .out15(decoder_1_out15), .out16(decoder_1_out16), .out17(decoder_1_out17),
    .sel(OPcode));  // open: out0, out1, out2, out3, out4, out5, out6, out7, out8, out9, out10, out11, out12, out13, out18, out19, out20, out21, out22, out23, out24, out25, out26, out27, out28, out29, out30, out31, en
  or or_2 (stall, decoder_1_out14, decoder_1_out15, decoder_1_out16, decoder_1_out17);

  assign IF_ID_RegEnable = Disable_PC;
  assign zero_signals = Disable_PC;
endmodule

module pipeline_processor (
  output [15:0] R1,
  output [15:0] R2,
  output [15:0] R3,
  output [15:0] R4,
  output [15:0] R5,
  output [15:0] R6,
  output [15:0] R7
);

  wire _0, _1, _2, _3, _4, _5, _6, _7, _8, _9, _10, _11, _12, _13, _14, _15, AluSrc, AluSrc1, AluSrc2,
       Branch, Clk, Disable_PC, extend_signal_1_extsignal, flush, IF_ID_enable, MemRd, MemRd1, MemRd2,
       MemRd3, MemWr, MemWr1, MemWr2, MemWr3, or_1_out, RegWr, RegWr1, RegWr2, RegWr3, RegWr4, zero_flag,
       Zero_Signals;
  wire [1:0] forwardA, forwardB, ForwardC, ForwardD, MemtoReg, MemtoReg1, MemtoReg2, MemtoReg3, RegDst,
       RegDst1, RegDst2, RegDst3;
  wire [2:0] branchSelector, RD1, Rd2, RD3, RD4, Rs2, Rt2;
  wire [3:0] ALUOP, ALUOP2;
  wire [15:0] ALUResult2, ALUResult3, bit_extender_2_out, bit_extender_3_out, bit_extender_4_out, BusA,
       BusA2, BusAB, BusB, BusB2, BusB3, BusBB, Data_store_2, Data_store_3, DataW, DataW4, imm2, imm11,
       imm16, LUI1, LUI2, LUI3, multiplexer_5_out, multiplexer_7_out, PC, PC_1, PC_2, PC_3, PC_3__1,
       PC_plus_1, ram_1_data, rom_1_data;

  PC_Counter pc_counter_1 (
    .PC_plus_1(PC_plus_1), .PC_value(PC), .busA__load_store(BusA), .Imm({_10, _9, _8, _7, _6}), .clk(Clk),
    .jump_0_10({_10, _9, _8, _7, _6, _5, _4, _3, _2, _1, _0}), .OPcode({_15, _14, _13, _12, _11}),
    .fun({_10, _9}), .branch_or_pc_1(Branch), .disable_PC(Disable_PC), .flush(flush), .PC_ID(PC_1));
  assign imm11 = {{5{_10}}, {_10, _9, _8, _7, _6, _5, _4, _3, _2, _1, _0}};  // Bit_Extender bit_extender_1
  // Probe on imm11
  // Probe on R1
  // Probe on R2
  // Probe on R3
  // Probe on R4
  // Probe on R5
  // Probe on R6
  // Probe on R7
  ROM #(.addrWidth(16), .dataWidth(16)) rom_1 (.addr(PC), .data(rom_1_data));  // open: sel
  stall stall_1 (
    .Rs({_5, _4, _3}), .OPcode({_15, _14, _13, _12, _11}), .RD2(Rd2), .Rt({_2, _1, _0}),
    .IF_ID_ALUSrc(AluSrc2), .IF_ID_RegEnable(IF_ID_enable), .Disable_PC(Disable_PC),
    .zero_signals(Zero_Signals));
  Clock clock_1 (.out(Clk));
  IF_ID_Reg if_id_reg_1 (
    .instruction(rom_1_data),
    .instruction_2({_15, _14, _13, _12, _11, _10, _9, _8, _7, _6, _5, _4, _3, _2, _1, _0}), .PC(PC),
    .PC1(PC_1), .IF_Flash(flush), .clock(Clk), .IF_ID_RegEnable(IF_ID_enable));
  branch_unit branch_unit_1 (.BusA(BusAB), .BusB(BusBB), .branchSelector(branchSelector), .Branch_enable(Branch));
  // Probe on {_5, _4, _3}
  Multiplexer #(.select(2), .width(3), .enable("false")) multiplexer_1 (
    .in0({_2, _1, _0}), .in1({_8, _7, _6}), .in2(3'b111), .in3(3'b001), .out(RD1), .sel(RegDst));
  // Probe on {_2, _1, _0}
  ControlUnit controlunit_1 (
    .OP5(_15), .OP4(_14), .OP3(_13), .OP2(_12), .OP1(_11), .RegDst1(RegDst[1]), .RegDst0(RegDst[0]),
    .RegWr(RegWr), .AluSrc(AluSrc), .MemRd(MemRd), .MemWr(MemWr), .memToReg1(MemtoReg[1]),
    .memToReg0(MemtoReg[0]), .BSelector2(branchSelector[2]), .BSelector1(branchSelector[1]),
    .BSelector0(branchSelector[0]));
  Register_File register_file_1 (
    .Read_Data_1(BusA), .Read_Data_2(BusB), .Write_Register(RD4), .Write_Data(DataW4),
    .Read_Register_1({_5, _4, _3}), .Read_Register_2({_2, _1, _0}), .Register_Write(RegWr4), .R1(R1),
    .R2(R2), .R3(R3), .R4(R4), .R5(R5), .R6(R6), .R7(R7));
  ALUCtrl aluctrl_1 (
    .OP4(_15), .OP3(_14), .OP2(_13), .OP1(_12), .OP0(_11), .F1(_10), .F0(_9), .ALU3(ALUOP[3]),
    .ALU2(ALUOP[2]), .ALU1(ALUOP[1]), .ALU0(ALUOP[0]));
  Forward_Unit_2 forward_unit_2_1 (
    .Rs({_5, _4, _3}), .Rd3(RD3), .Rd4(RD4), .RegWr3(RegWr3), .RegWr4(RegWr4), .Rt({_2, _1, _0}),
    .Forward_C(ForwardC), .Forward_D(ForwardD));
  Multiplexer #(.select(2), .width(16), .enable("false")) multiplexer_2 (
    .in0(BusA), .in1(DataW), .in2(DataW4), .out(BusAB), .sel(ForwardC));  // open: in3
  Multiplexer #(.select(2), .width(16), .enable("false")) multiplexer_3 (
    .in0(BusB), .in1(DataW), .in2(DataW4), .out(BusBB), .sel(ForwardD));  // open: in3
  LUI lui_1 (.jump_0_10(bit_extender_2_out), .out_2(LUI1));
  assign bit_extender_2_out = {{5{_10}}, {_10, _9, _8, _7, _6, _5, _4, _3, _2, _1, _0}};  // Bit_Extender bit_extender_2
  Multiplexer #(.width(8), .enable("false")) multiplexer_4 (
    .in0({MemtoReg, MemWr, MemRd, AluSrc, RegWr, RegDst}), .in1({8{1'b0}}),
    .out({MemtoReg1, MemWr1, MemRd1, AluSrc1, RegWr1, RegDst1}), .sel(Zero_Signals));
  ID_EX_Reg id_ex_reg_1 (
    .PC1(PC_1), .LUI(LUI1), .RegDst(RegDst1), .ALUSrc(AluSrc1), .BUSA(BusA), .RegWr(RegWr1), .BUSB(BusB),
    .MemRd(MemRd1), .MemWr(MemWr1), .Rd1(RD1), .MemtoReg(MemtoReg1), .Imm(imm16), .Alu_op(ALUOP),
    .Rs({_5, _4, _3}), .Rt({_2, _1, _0}), .PC2(PC_2), .LUI_2(LUI2), .RegDst_2(RegDst2), .BUSA_2(BusA2),
    .ALUSrc_2(AluSrc2), .RegWr_2(RegWr2), .BUSB_2(BusB2), .MemRd_2(MemRd2), .MemWr_2(MemWr2), .Rd1_2(Rd2),
    .MemtoReg_2(MemtoReg2), .Imm_2(imm2), .Alu_op_2(ALUOP2), .Rs_2(Rs2), .Rt_2(Rt2), .in_16(Clk));
  Multiplexer #(.select(2), .width(16), .enable("false")) multiplexer_5 (
    .in0(BusA2), .in1(DataW), .in2(DataW4), .out(multiplexer_5_out), .sel(forwardA));  // open: in3
  Multiplexer #(.select(2), .width(16), .enable("false")) multiplexer_6 (
    .in0(BusB2), .in1(DataW), .in2(DataW4), .out(Data_store_2), .sel(forwardB));  // open: in3
  Forward_Unit forward_unit_1 (
    .ID_EX_RS2(Rs2), .EXE_MEM_RD3(RD3), .EX_MEM_REG_WR(RegWr3), .ID_EX_RT2(Rt2), .WB_RD4(RD4),
    .FORWARDA(forwardA), .MEM_WB_REG_WR(RegWr4), .out_8(forwardB));
  Multiplexer #(.width(16), .enable("false")) multiplexer_7 (
    .in0(Data_store_2), .in1(imm2), .out(multiplexer_7_out), .sel(AluSrc2));
  ALU alu_1 (.A(multiplexer_5_out), .B(multiplexer_7_out), .zeroFlag(zero_flag), .R(ALUResult2), .func(ALUOP2));
  assign bit_extender_3_out = {{11{_10}}, {_10, _9, _8, _7, _6}};  // Bit_Extender bit_extender_3
  assign bit_extender_4_out = {{11{1'b0}}, {_10, _9, _8, _7, _6}};  // Bit_Extender bit_extender_4
  Multiplexer #(.width(16), .enable("false")) multiplexer_8 (
    .in0(bit_extender_3_out), .in1(bit_extender_4_out), .out(imm16), .sel(extend_signal_1_extsignal));
  extend_signal extend_signal_1 (
    .OP4(_15), .OP3(_14), .OP2(_13), .OP1(_12), .OP0(_11), .Extsignal(extend_signal_1_extsignal));
  EX_DM_Reg ex_dm_reg_1 (
    .clk(Clk), .ALU_Result(ALUResult2), .RegDst(RegDst2), .Rd2(Rd2), .RegWr(RegWr2), .Bus_B(BusB2),
    .MemRd(MemRd2), .PC3(PC_2), .MemWr(MemWr2), .LUI(LUI2), .MemtoReg(MemtoReg2), .ALU_Result_2(ALUResult3),
    .RegDst_2(RegDst3), .Rd2_2(RD3), .RegWr_2(RegWr3), .Bus_B_2(BusB3), .MemRd_2(MemRd3), .PC4(PC_3),
    .MemWr_2(MemWr3), .LUI_2(LUI3), .MemtoReg_2(MemtoReg3), .Data_Load_2(Data_store_2),
    .Data_Load_3(Data_store_3));
  or or_1 (or_1_out, MemWr3, MemRd3);
  RAM #(.addrWidth(16), .dataWidth(16), .bus("separate")) ram_1 (
    .addr(ALUResult3), .din(Data_store_3), .data(ram_1_data), .str(MemWr3), .sel(or_1_out), .clk(Clk),
    .ld(MemRd3));  // open: clr
  Adder #(.width(16)) adder_1 (.a(PC_3), .b(16'h1), .out(PC_3__1));  // open: cin, cout
  Multiplexer #(.select(2), .width(16), .enable("false")) multiplexer_9 (
    .in0(ALUResult3), .in1(ram_1_data), .in2(PC_3__1), .in3(LUI3), .out(DataW), .sel(MemtoReg3));
  DM_WB_Reg dm_wb_reg_1 (
    .clk(Clk), .DataW(DataW), .Rd3(RD3), .RegWr(RegWr3), .DataW_2(DataW4), .Rd3_2(RD4), .RegWr_2(RegWr4));

  // Other names for the same wires on the sheet: OP_code[4:0] = {_15, _14, _13, _12, _11};
  //   imm5[4:0] = {_10, _9, _8, _7, _6}; jump_0_10[10:0] = {_10, _9, _8, _7, _6, _5, _4, _3, _2, _1, _0};
  //   offset_0_4[4:0] = {_10, _9, _8, _7, _6}; Rd[2:0] = {_8, _7, _6}; Func[1:0] = {_10, _9}; Rs[2:0] = {_5, _4, _3};
  //   Rt[2:0] = {_2, _1, _0}

  // Notes on the sheet:
  //   instruction MEM
  //   contents of rom_1 (hex, n*v repeats v):
  //   9384 3b4d 4cd 6001 6042 6083 3aa4 b24 914 d93 70f0 88a 7700 6804 f804 4193 58de 7000 353 6001 614a
  //   618b 113 6804 1038
  //   STALL UNIT
  //   Branch check Unit
  //   ALU operation signal
  //   immediate extend unit
  //   PC+1 for JAL
endmodule

module Forward_Unit_2 (
  input  [2:0] Rs,
  input  [2:0] Rt,
  input  [2:0] Rd3,
  input  [2:0] Rd4,
  input  RegWr3,
  input  RegWr4,
  output [1:0] Forward_C,
  output [1:0] Forward_D
);

  wire and_1_out, and_2_out, and_3_out, and_4_out, comparator_1_eq, comparator_2_eq, comparator_3_eq,
       comparator_4_eq, comparator_5_eq, comparator_6_eq, comparator_7_eq, comparator_8_eq, not_1_out,
       not_2_out;

  Comparator #(.width(3), .mode("unsigned")) comparator_1 (.a(Rt), .b(Rd4), .eq(comparator_1_eq));  // open: gt, lt
  Comparator #(.width(3), .mode("unsigned")) comparator_2 (.a(Rt), .b(3'b000), .eq(comparator_2_eq));  // open: gt, lt
  Comparator #(.width(3), .mode("unsigned")) comparator_3 (.a(Rs), .b(Rd3), .eq(comparator_3_eq));  // open: gt, lt
  not not_1 (not_1_out, comparator_4_eq);
  Comparator #(.width(3), .mode("unsigned")) comparator_4 (.a(Rs), .b(3'b000), .eq(comparator_4_eq));  // open: gt, lt
  Comparator #(.width(3), .mode("unsigned")) comparator_5 (.a(Rs), .b(Rd4), .eq(comparator_5_eq));  // open: gt, lt
  Comparator #(.width(3), .mode("unsigned")) comparator_6 (.a(Rs), .b(3'b000), .eq(comparator_6_eq));  // open: gt, lt
  Comparator #(.width(3), .mode("unsigned")) comparator_7 (.a(Rt), .b(Rd3), .eq(comparator_7_eq));  // open: gt, lt
  not not_2 (not_2_out, comparator_8_eq);
  Comparator #(.width(3), .mode("unsigned")) comparator_8 (.a(Rt), .b(3'b000), .eq(comparator_8_eq));  // open: gt, lt
  and and_1 (and_1_out, comparator_3_eq, not_1_out, RegWr3);
  and and_2 (and_2_out, comparator_5_eq, comparator_6_eq, RegWr4);
  and and_3 (and_3_out, comparator_7_eq, not_2_out, RegWr3);
  and and_4 (and_4_out, comparator_1_eq, comparator_2_eq, RegWr4);
  Forward_Correct forward_correct_1 (.a0(and_1_out), .a1(and_2_out), .f0(Forward_C[1]), .f1(Forward_C[0]));
  Forward_Correct forward_correct_2 (.a0(and_3_out), .a1(and_4_out), .f0(Forward_D[1]), .f1(Forward_D[0]));
endmodule

module Forward_Correct (
  input  a0,
  input  a1,
  output f0,
  output f1
);

  wire not_1_out;

  not not_1 (not_1_out, a0);
  and and_1 (f0, not_1_out, a1);

  assign f1 = a0;
endmodule
